# Fritzing sketch Mandala (saved by Fritzing 0.9.3b)
breadboards: 1

parts:
  Part1 = Arduino Uno (Rev3)
  J1 = Basic Servo
  J2 = Basic Servo
  Matrix_keypad2 = KEYPAD 4x4

nets:
  N1: Part1.D8, Matrix_keypad2.row2
  N2: Part1.D9_PWM, Matrix_keypad2.row1
  N3: Part1.D10_PWM/SS, Matrix_keypad2.col4
  N4: Part1.D11_PWM/MOSI, Matrix_keypad2.col3
  N5: Part1.D12/MISO, Matrix_keypad2.col2
  N6: Part1.D13/SCK, Matrix_keypad2.col1
  N7: Part1.D2, J2.pulse
  N8: Part1.D4, J1.pulse
  N9: Part1.D6_PWM, Matrix_keypad2.row4
  N10: Part1.D7, Matrix_keypad2.row3
  VCC: Part1.5V, J1.vcc, J2.vcc
  GND: Part1.GND, J1.gnd

custom parts:
  KEYPAD 4x4: Matrix keypad 16 buttons, 4 rows x 4 columns
